# Fritzing sketch Simply Amazing PID (saved by Fritzing 0.9.3b)
circuit board: 5.48692cm x 3.22824cm
breadboards: 1

parts:
  R1 = Resistor [tolerance=±5% resistance=4.7k package=THT]
  U1 = RELAY-SOLIDSTATE [package=relay-s108t02]
  V1 = AC Power [voltage=5 frequency=60]
  R2 = Resistor [tolerance=±5% resistance=470 package=THT]
  DS2 = DS18B20 1-Wire Temperature Sensor [part_number=DS18B20]
  Q1 = TRANSISTOR_NPN [part_number=2N2222A package=to-92]
  R4 = Resistor [tolerance=±5% resistance=1k package=THT]
  R5 = Resistor [tolerance=±5% resistance=10k package=THT]
  R6 = Resistor [tolerance=±5% resistance=10k package=THT]
  R3 = Resistor [tolerance=±5% resistance=1k package=THT]
  S1 = Taiway 100-SP-X-T1 SPDT Miniature Toggle Switch [part_number=100-SP-X-T1-0-0-B1-M1 package=THT]
  S2 = SWITCH-MOMENTARY-2 [package=tactile-pth]  # not connected
  MCU1 = Raspberry Pi Zero

nets:
  N1: R1.Pin_0, DS2.VDD, S1.COM, MCU1.pin_1
  N2: R1.Pin_1, DS2.DQ, MCU1.pin_7
  N3: U1.T1, V1.V-
  N4: U1.+, MCU1.pin_2
  N5: U1.-, Q1.C
  N6: R2.Pin_0, Q1.B
  N7: R2.Pin_1, MCU1.pin_40
  N8: DS2.GND, Q1.E, R5.Pin_1, R6.Pin_1, MCU1.pin_9, MCU1.pin_20, MCU1.pin_25, MCU1.pin_30, MCU1.pin_39
  N9: R4.Pin_0, R6.Pin_0, S1.L1
  N10: R4.Pin_1, MCU1.pin_19
  N11: R5.Pin_0, R3.Pin_0, S1.L2
  N12: R3.Pin_1, MCU1.pin_21
